// Logisim project Assignment3_task3.1.circ as structural Verilog: 1 circuit, main circuit main
module main (
  input  Cin,
  input  [3:0] A,
  input  [3:0] B,
  output [3:0] S,
  output out_5
);

  Adder #(.width(4)) adder_1 (.a(A), .b(B), .out(S), .cin(Cin), .cout(out_5));
endmodule
