// Logisim project Assignment3_task3.2.circ as structural Verilog: 1 circuit, main circuit main
module main (
  input  [3:0] A,
  input  [3:0] B,
  input  Cin,
  input  [3:0] S,
  output Cout
);

  wire adder_1_cout, adder_2_cout, adder_3_cout;

  Adder #(.width(1)) adder_1 (.a(B[0]), .b(A[0]), .out(S[0]), .cin(Cin), .cout(adder_1_cout));
  Adder #(.width(1)) adder_2 (.a(B[1]), .b(A[1]), .out(S[1]), .cin(adder_1_cout), .cout(adder_2_cout));
  Adder #(.width(1)) adder_3 (.a(B[2]), .b(A[2]), .out(S[2]), .cin(adder_2_cout), .cout(adder_3_cout));
  Adder #(.width(1)) adder_4 (.a(B[3]), .b(A[3]), .out(S[3]), .cin(adder_3_cout), .cout(Cout));
endmodule
