// Logisim project Assignment4_5.circ as structural Verilog: 3 circuits, main circuit main
module main (
  input  CLK,
  input  D,
  output Q,
  output Q_prime
);

  wire and_1_out, and_2_out, not_1_out;

  and and_1 (and_1_out, CLK, not_1_out);
  not not_1 (not_1_out, D);
  and and_2 (and_2_out, CLK, D);
  nor nor_1 (Q, and_1_out, Q_prime);
  nor nor_2 (Q_prime, Q, and_2_out);
endmodule

module D_flip_flop (
  input  in_1,
  input  Din,
  output Q
);

  wire Master_q, not_1_out;

  not not_1 (not_1_out, in_1);
  main Master (.CLK(not_1_out), .D(Din), .Q(Master_q));  // open: Q_prime
  main Slave (.CLK(in_1), .D(Master_q), .Q(Q));  // open: Q_prime
endmodule

module _4_bit_register (
  input  CLK,
  input  [3:0] X,
  output [3:0] Y
);

  D_flip_flop d_flip_flop_1 (.in_1(CLK), .Din(X[0]), .Q(Y[0]));
  D_flip_flop d_flip_flop_2 (.in_1(CLK), .Din(X[1]), .Q(Y[1]));
  D_flip_flop d_flip_flop_3 (.in_1(CLK), .Din(X[2]), .Q(Y[2]));
  D_flip_flop d_flip_flop_4 (.in_1(CLK), .Din(X[3]), .Q(Y[3]));
endmodule
